// Logisim project main.circ as structural Verilog
module main (
  input  Choose_level
);

  wire cdm_8_1_p2, cdm_8_1_p4, cdm_8_1_p5, cdm_8_1_p6, cdm_8_1_p7, cdm_8_1_p8, cdm_8_1_p9, cdm_8_1_p10, Cl,
       code, data, decoder_1_out0, decoder_3_out0, decoder_4_out0, decoder_5_out0, DN_out, FA_out, FB_out,
       FE_out, FF_out, I_Osel, In_out_prime, mem, nand_1_out, not_1_out, not_2_out, RAM, reset, Rset, UP_out;
  wire [1:0] joystick_1_y;
  wire [3:0] I_Oadr;
  wire [4:0] kinematic_controller_1_ballx, kinematic_controller_1_bally, kinematic_controller_1_chipid,
       kinematic_controller_1_leftbaty, kinematic_controller_1_rightbaty;
  wire [7:0] cdm_8_1_p14, cdm_8_1_p15, I_Odat, lScore, register_1_q, register_2_q, register_3_q, rScore,
       undriven;
  wire [7:4] cdm_8_1_p13;
  wire [31:0] n32cells_1_out_6, n32cells_1_out_7, n32cells_1_out_8, n32cells_1_out_9, n32cells_1_out_10,
       n32cells_1_out_11, n32cells_1_out_12, n32cells_1_out_13, n32cells_1_out_14, n32cells_1_out_15,
       n32cells_1_out_16, n32cells_1_out_17, n32cells_1_out_18, n32cells_1_out_19, n32cells_1_out_20,
       n32cells_1_out_21, n32cells_1_out_22, n32cells_1_out_23, n32cells_1_out_24, n32cells_1_out_25,
       n32cells_1_out_26, n32cells_1_out_27, n32cells_1_out_28, n32cells_1_out_29, n32cells_1_out_30,
       n32cells_1_out_31, n32cells_1_out_32, n32cells_1_out_33, n32cells_1_out_34, n32cells_1_out_35,
       n32cells_1_out_36, n32cells_1_out_37;

  Button UP (.out(UP_out));
  Button DN (.out(DN_out));
  Button R (.out(reset));
  // Probe on I_Oadr
  Hex_Digit_Display hex_digit_display_1 (.value(lScore[3:0]));  // open: dp
  Joystick #(.bits(2)) joystick_1 (.y(joystick_1_y));  // open: x
  _32cells u_32cells_1 (
    .chipID(kinematic_controller_1_chipid), .ballX(kinematic_controller_1_ballx),
    .ballY(kinematic_controller_1_bally), .leftbatY(kinematic_controller_1_leftbaty),
    .rightbatY(kinematic_controller_1_rightbaty), .out_6(n32cells_1_out_6), .out_22(n32cells_1_out_22),
    .out_7(n32cells_1_out_7), .out_23(n32cells_1_out_23), .out_8(n32cells_1_out_8),
    .out_24(n32cells_1_out_24), .out_9(n32cells_1_out_9), .out_25(n32cells_1_out_25),
    .out_10(n32cells_1_out_10), .out_26(n32cells_1_out_26), .out_11(n32cells_1_out_11),
    .out_27(n32cells_1_out_27), .out_12(n32cells_1_out_12), .out_28(n32cells_1_out_28),
    .out_13(n32cells_1_out_13), .out_29(n32cells_1_out_29), .out_14(n32cells_1_out_14),
    .out_30(n32cells_1_out_30), .out_15(n32cells_1_out_15), .out_31(n32cells_1_out_31),
    .out_16(n32cells_1_out_16), .out_32(n32cells_1_out_32), .out_17(n32cells_1_out_17),
    .out_33(n32cells_1_out_33), .out_18(n32cells_1_out_18), .out_34(n32cells_1_out_34),
    .out_19(n32cells_1_out_19), .out_35(n32cells_1_out_35), .out_20(n32cells_1_out_20),
    .out_36(n32cells_1_out_36), .out_21(n32cells_1_out_21), .out_37(n32cells_1_out_37));
  DotMatrix #(.matrixcols(32), .matrixrows(32)) dotmatrix_1 (
    .col0(n32cells_1_out_6), .col1(n32cells_1_out_22), .col2(n32cells_1_out_7), .col3(n32cells_1_out_23),
    .col4(n32cells_1_out_8), .col5(n32cells_1_out_24), .col6(n32cells_1_out_9), .col7(n32cells_1_out_25),
    .col8(n32cells_1_out_10), .col9(n32cells_1_out_26), .col10(n32cells_1_out_11), .col11(n32cells_1_out_27),
    .col12(n32cells_1_out_12), .col13(n32cells_1_out_28), .col14(n32cells_1_out_13),
    .col15(n32cells_1_out_29), .col16(n32cells_1_out_14), .col17(n32cells_1_out_30),
    .col18(n32cells_1_out_15), .col19(n32cells_1_out_31), .col20(n32cells_1_out_16),
    .col21(n32cells_1_out_32), .col22(n32cells_1_out_17), .col23(n32cells_1_out_33),
    .col24(n32cells_1_out_18), .col25(n32cells_1_out_34), .col26(n32cells_1_out_19),
    .col27(n32cells_1_out_35), .col28(n32cells_1_out_20), .col29(n32cells_1_out_36),
    .col30(n32cells_1_out_21), .col31(n32cells_1_out_37));
  kinematic_controller kinematic_controller_1 (
    .chipID(kinematic_controller_1_chipid), .ballX(kinematic_controller_1_ballx),
    .ballY(kinematic_controller_1_bally), .leftbatY(kinematic_controller_1_leftbaty),
    .rightbatY(kinematic_controller_1_rightbaty), .reset(reset), .Rscores(rScore), .clock(Cl),
    .Lscores(lScore), .joystick(joystick_1_y), .up(UP_out), .down(DN_out), .Choose_level(Choose_level));  // open: rightBat
  Button u_Choose_level ();  // open: out
  Hex_Digit_Display hex_digit_display_2 (.value(rScore[3:0]));  // open: dp
  Clock clock_1 (.out(Cl));
  // Probe on cdm_8_1_p5
  // Probe on cdm_8_1_p2
  // Probe on cdm_8_1_p4
  // Probe on cdm_8_1_p6
  Button button_1 (.out(Rset));
  and and_1 (I_Osel, not_1_out, Cl, data);
  // Probe on cdm_8_1_p8
  // Probe on cdm_8_1_p7
  // Probe on cdm_8_1_p9
  // CdM_8 cdm_8_1: pin names not known; wires that end beside it: Cl, cdm_8_1_p2, Rset, cdm_8_1_p4, cdm_8_1_p5, cdm_8_1_p6, cdm_8_1_p7, cdm_8_1_p8, cdm_8_1_p9, cdm_8_1_p10, mem, In_out_prime, {cdm_8_1_p13, I_Oadr}, cdm_8_1_p14, cdm_8_1_p15
  not not_1 (not_1_out, nand_1_out);
  nand nand_1 (nand_1_out, cdm_8_1_p13[4], cdm_8_1_p13[5], cdm_8_1_p13[6], cdm_8_1_p13[7]);
  and and_2 (RAM, nand_1_out, data);
  Register register_1 (.D(I_Odat), .Q(register_1_q), .clk(decoder_1_out0));  // open: en, clr
  // Probe on register_1_q
  assign I_Odat = not_2_out ? cdm_8_1_p14 : 8'bz;  // Controlled_Buffer controlled_buffer_1
  not not_2 (not_2_out, In_out_prime);
  assign cdm_8_1_p15 = In_out_prime ? I_Odat : 8'bz;  // Controlled_Buffer controlled_buffer_2
  and FE (FE_out, I_Osel, ~I_Oadr[0], I_Oadr[1], I_Oadr[2], I_Oadr[3]);  // AND_Gate
  Decoder #(.disabled(0)) decoder_1 (.out0(decoder_1_out0), .sel(In_out_prime), .en(FE_out));  // open: out1
  // Probe on register_1_q[7:3]
  Decoder decoder_2 (.out0(code), .out1(data), .sel(cdm_8_1_p10), .en(mem));
  // Probe on {cdm_8_1_p13, I_Oadr}
  Register register_2 (.D(I_Odat), .Q(register_2_q), .clk(decoder_3_out0));  // open: en, clr
  Pull_Resistor pull_resistor_1 (.node(I_Oadr[0]));
  Pull_Resistor pull_resistor_2 (.node(I_Oadr[1]));
  Pull_Resistor pull_resistor_3 (.node(I_Oadr[2]));
  Pull_Resistor pull_resistor_4 (.node(I_Oadr[3]));
  Pull_Resistor pull_resistor_5 (.node(cdm_8_1_p13[4]));
  Pull_Resistor pull_resistor_6 (.node(cdm_8_1_p13[5]));
  Pull_Resistor pull_resistor_7 (.node(cdm_8_1_p13[6]));
  Pull_Resistor pull_resistor_8 (.node(cdm_8_1_p13[7]));
  and FF (FF_out, I_Osel, I_Oadr[0], I_Oadr[1], I_Oadr[2], I_Oadr[3]);
  Decoder #(.disabled(0)) decoder_3 (.out0(decoder_3_out0), .sel(In_out_prime), .en(FF_out));  // open: out1
  // Probe on register_2_q[7:3]
  ROM rom_1 (.addr({cdm_8_1_p13, I_Oadr}), .data(I_Odat), .sel(code));
  RAM ram_1 (.addr({cdm_8_1_p13, I_Oadr}), .data(I_Odat), .sel(RAM), .clk(Cl), .ld(In_out_prime));  // open: clr
  assign I_Odat = decoder_4_out0 ? undriven : 8'bz;  // Controlled_Buffer controlled_buffer_3
  and FA (FA_out, I_Osel, ~I_Oadr[0], I_Oadr[1], ~I_Oadr[2], I_Oadr[3]);  // AND_Gate
  Decoder #(.disabled(0)) decoder_4 (.out0(decoder_4_out0), .sel(In_out_prime), .en(FA_out));  // open: out1
  Register register_3 (.D(I_Odat), .Q(register_3_q), .clk(decoder_5_out0));  // open: en, clr
  and FB (FB_out, I_Osel, I_Oadr[0], I_Oadr[1], ~I_Oadr[2], I_Oadr[3]);  // AND_Gate
  Decoder #(.disabled(0)) decoder_5 (.out0(decoder_5_out0), .sel(In_out_prime), .en(FB_out));  // open: out1

  // Other names for the same wires on the sheet: rd_wr_prime = In_out_prime

  // Notes on the sheet:
  //   BallX
  //   BallY
  //   instr memory
  //   data memory
  //   Left Bat
  //   Right Bat
endmodule

module _32cells (
  input  [4:0] chipID,
  input  [4:0] ballX,
  input  [4:0] ballY,
  input  [4:0] leftbatY,
  input  [4:0] rightbatY,
  output [31:0] out_6,
  output [31:0] out_7,
  output [31:0] out_8,
  output [31:0] out_9,
  output [31:0] out_10,
  output [31:0] out_11,
  output [31:0] out_12,
  output [31:0] out_13,
  output [31:0] out_14,
  output [31:0] out_15,
  output [31:0] out_16,
  output [31:0] out_17,
  output [31:0] out_18,
  output [31:0] out_19,
  output [31:0] out_20,
  output [31:0] out_21,
  output [31:0] out_22,
  output [31:0] out_23,
  output [31:0] out_24,
  output [31:0] out_25,
  output [31:0] out_26,
  output [31:0] out_27,
  output [31:0] out_28,
  output [31:0] out_29,
  output [31:0] out_30,
  output [31:0] out_31,
  output [31:0] out_32,
  output [31:0] out_33,
  output [31:0] out_34,
  output [31:0] out_35,
  output [31:0] out_36,
  output [31:0] out_37
);

  wire [4:0] n8cells_1_ballx_2, n8cells_1_bally_2, n8cells_1_chipid_2, n8cells_1_leftbaty_2,
       n8cells_1_rightbaty_2, n8cells_2_ballx_2, n8cells_2_bally_2, n8cells_2_chipid_2, n8cells_2_leftbaty_2,
       n8cells_2_rightbaty_2, n8cells_3_ballx_2, n8cells_3_bally_2, n8cells_3_chipid_2, n8cells_3_leftbaty_2,
       n8cells_3_rightbaty_2;

  _8cells u_8cells_1 (
    .chipID(chipID), .ballX(ballX), .ballY(ballY), .leftbatY(leftbatY), .rightbatY(rightbatY),
    .chipID_2(n8cells_1_chipid_2), .ballX_2(n8cells_1_ballx_2), .ballY_2(n8cells_1_bally_2),
    .leftbatY_2(n8cells_1_leftbaty_2), .rightbatY_2(n8cells_1_rightbaty_2), .out_6(out_6), .out_7(out_22),
    .out_8(out_7), .out_9(out_23), .out_10(out_8), .out_11(out_24), .out_12(out_9), .out_13(out_25));
  _8cells u_8cells_2 (
    .chipID(n8cells_1_chipid_2), .ballX(n8cells_1_ballx_2), .ballY(n8cells_1_bally_2),
    .leftbatY(n8cells_1_leftbaty_2), .rightbatY(n8cells_1_rightbaty_2), .chipID_2(n8cells_2_chipid_2),
    .ballX_2(n8cells_2_ballx_2), .ballY_2(n8cells_2_bally_2), .leftbatY_2(n8cells_2_leftbaty_2),
    .rightbatY_2(n8cells_2_rightbaty_2), .out_6(out_10), .out_7(out_26), .out_8(out_11), .out_9(out_27),
    .out_10(out_12), .out_11(out_28), .out_12(out_13), .out_13(out_29));
  _8cells u_8cells_3 (
    .chipID(n8cells_2_chipid_2), .ballX(n8cells_2_ballx_2), .ballY(n8cells_2_bally_2),
    .leftbatY(n8cells_2_leftbaty_2), .rightbatY(n8cells_2_rightbaty_2), .chipID_2(n8cells_3_chipid_2),
    .ballX_2(n8cells_3_ballx_2), .ballY_2(n8cells_3_bally_2), .leftbatY_2(n8cells_3_leftbaty_2),
    .rightbatY_2(n8cells_3_rightbaty_2), .out_6(out_14), .out_7(out_30), .out_8(out_15), .out_9(out_31),
    .out_10(out_16), .out_11(out_32), .out_12(out_17), .out_13(out_33));
  _8cells u_8cells_4 (
    .chipID(n8cells_3_chipid_2), .ballX(n8cells_3_ballx_2), .ballY(n8cells_3_bally_2),
    .leftbatY(n8cells_3_leftbaty_2), .rightbatY(n8cells_3_rightbaty_2), .out_6(out_18), .out_7(out_34),
    .out_8(out_19), .out_9(out_35), .out_10(out_20), .out_11(out_36), .out_12(out_21), .out_13(out_37));  // open: chipID_2, ballX_2, ballY_2, leftbatY_2, rightbatY_2
endmodule

module _8cells (
  input  [4:0] chipID,
  input  [4:0] ballX,
  input  [4:0] ballY,
  input  [4:0] leftbatY,
  input  [4:0] rightbatY,
  output [31:0] out_6,
  output [31:0] out_7,
  output [31:0] out_8,
  output [31:0] out_9,
  output [31:0] out_10,
  output [31:0] out_11,
  output [31:0] out_12,
  output [31:0] out_13,
  output [4:0] chipID_2,
  output [4:0] ballX_2,
  output [4:0] ballY_2,
  output [4:0] leftbatY_2,
  output [4:0] rightbatY_2
);

  wire [4:0] n1cell_1_out_7, n1cell_1_out_8, n1cell_1_out_9, n1cell_1_out_10, n1cell_1_out_11,
       n1cell_2_out_7, n1cell_2_out_8, n1cell_2_out_9, n1cell_2_out_10, n1cell_2_out_11, n1cell_3_out_7,
       n1cell_3_out_8, n1cell_3_out_9, n1cell_3_out_10, n1cell_3_out_11, n1cell_4_out_7, n1cell_4_out_8,
       n1cell_4_out_9, n1cell_4_out_10, n1cell_4_out_11, n1cell_5_out_7, n1cell_5_out_8, n1cell_5_out_9,
       n1cell_5_out_10, n1cell_5_out_11, n1cell_6_out_7, n1cell_6_out_8, n1cell_6_out_9, n1cell_6_out_10,
       n1cell_6_out_11, n1cell_7_out_7, n1cell_7_out_8, n1cell_7_out_9, n1cell_7_out_10, n1cell_7_out_11;

  _1cell u_1cell_1 (
    .chipID(chipID), .ballX(ballX), .ballY(ballY), .leftbatY(leftbatY), .rightbatY(rightbatY),
    .out_7(n1cell_1_out_7), .out_8(n1cell_1_out_8), .out_9(n1cell_1_out_9), .out_10(n1cell_1_out_10),
    .out_11(n1cell_1_out_11), .out_6(out_6));
  _1cell u_1cell_2 (
    .chipID(n1cell_1_out_7), .ballX(n1cell_1_out_8), .ballY(n1cell_1_out_9), .leftbatY(n1cell_1_out_10),
    .rightbatY(n1cell_1_out_11), .out_7(n1cell_2_out_7), .out_8(n1cell_2_out_8), .out_9(n1cell_2_out_9),
    .out_10(n1cell_2_out_10), .out_11(n1cell_2_out_11), .out_6(out_7));
  _1cell u_1cell_3 (
    .chipID(n1cell_2_out_7), .ballX(n1cell_2_out_8), .ballY(n1cell_2_out_9), .leftbatY(n1cell_2_out_10),
    .rightbatY(n1cell_2_out_11), .out_7(n1cell_3_out_7), .out_8(n1cell_3_out_8), .out_9(n1cell_3_out_9),
    .out_10(n1cell_3_out_10), .out_11(n1cell_3_out_11), .out_6(out_8));
  _1cell u_1cell_4 (
    .chipID(n1cell_3_out_7), .ballX(n1cell_3_out_8), .ballY(n1cell_3_out_9), .leftbatY(n1cell_3_out_10),
    .rightbatY(n1cell_3_out_11), .out_7(n1cell_4_out_7), .out_8(n1cell_4_out_8), .out_9(n1cell_4_out_9),
    .out_10(n1cell_4_out_10), .out_11(n1cell_4_out_11), .out_6(out_9));
  _1cell u_1cell_5 (
    .chipID(n1cell_4_out_7), .ballX(n1cell_4_out_8), .ballY(n1cell_4_out_9), .leftbatY(n1cell_4_out_10),
    .rightbatY(n1cell_4_out_11), .out_7(n1cell_5_out_7), .out_8(n1cell_5_out_8), .out_9(n1cell_5_out_9),
    .out_10(n1cell_5_out_10), .out_11(n1cell_5_out_11), .out_6(out_10));
  _1cell u_1cell_6 (
    .chipID(n1cell_5_out_7), .ballX(n1cell_5_out_8), .ballY(n1cell_5_out_9), .leftbatY(n1cell_5_out_10),
    .rightbatY(n1cell_5_out_11), .out_7(n1cell_6_out_7), .out_8(n1cell_6_out_8), .out_9(n1cell_6_out_9),
    .out_10(n1cell_6_out_10), .out_11(n1cell_6_out_11), .out_6(out_11));
  _1cell u_1cell_7 (
    .chipID(n1cell_6_out_7), .ballX(n1cell_6_out_8), .ballY(n1cell_6_out_9), .leftbatY(n1cell_6_out_10),
    .rightbatY(n1cell_6_out_11), .out_7(n1cell_7_out_7), .out_8(n1cell_7_out_8), .out_9(n1cell_7_out_9),
    .out_10(n1cell_7_out_10), .out_11(n1cell_7_out_11), .out_6(out_12));
  _1cell u_1cell_8 (
    .chipID(n1cell_7_out_7), .ballX(n1cell_7_out_8), .ballY(n1cell_7_out_9), .leftbatY(n1cell_7_out_10),
    .rightbatY(n1cell_7_out_11), .out_7(chipID_2), .out_8(ballX_2), .out_9(ballY_2), .out_10(leftbatY_2),
    .out_11(rightbatY_2), .out_6(out_13));
endmodule

module _1cell (
  input  [4:0] chipID,
  input  [4:0] ballX,
  input  [4:0] ballY,
  input  [4:0] leftbatY,
  input  [4:0] rightbatY,
  output [31:0] out_6,
  output [4:0] out_7,
  output [4:0] out_8,
  output [4:0] out_9,
  output [4:0] out_10,
  output [4:0] out_11
);

  wire comparator_1_eq, comparator_1_gt, comparator_1_lt, comparator_2_eq, comparator_2_gt, comparator_2_lt,
       comparator_3_eq, comparator_3_gt, comparator_3_lt, or_1_out, or_2_out, or_4_out;
  wire [31:0] ball, decoder_1_out0, decoder_2_out0, decoder_3_out0, lbat_t, multiplier_1_out,
       multiplier_2_out, rbat_t;

  // Probe on 5'b00011
  // Probe on 5'b11100
  // Probe on leftbatY
  Comparator #(.width(5)) comparator_1 (
    .a(chipID), .b(ballX), .gt(comparator_1_gt), .eq(comparator_1_eq), .lt(comparator_1_lt));
  Decoder #(.select(5), .enable("false")) decoder_1 (
    .out0(decoder_1_out0[0]), .out1(decoder_1_out0[1]), .out2(decoder_1_out0[2]), .out3(decoder_1_out0[3]),
    .out4(decoder_1_out0[4]), .out5(decoder_1_out0[5]), .out6(decoder_1_out0[6]), .out7(decoder_1_out0[7]),
    .out8(decoder_1_out0[8]), .out9(decoder_1_out0[9]), .out10(decoder_1_out0[10]),
    .out11(decoder_1_out0[11]), .out12(decoder_1_out0[12]), .out13(decoder_1_out0[13]),
    .out14(decoder_1_out0[14]), .out15(decoder_1_out0[15]), .out16(decoder_1_out0[16]),
    .out17(decoder_1_out0[17]), .out18(decoder_1_out0[18]), .out19(decoder_1_out0[19]),
    .out20(decoder_1_out0[20]), .out21(decoder_1_out0[21]), .out22(decoder_1_out0[22]),
    .out23(decoder_1_out0[23]), .out24(decoder_1_out0[24]), .out25(decoder_1_out0[25]),
    .out26(decoder_1_out0[26]), .out27(decoder_1_out0[27]), .out28(decoder_1_out0[28]),
    .out29(decoder_1_out0[29]), .out30(decoder_1_out0[30]), .out31(decoder_1_out0[31]), .sel(ballY));
  Comparator #(.width(5)) comparator_2 (
    .a(chipID), .b(5'b00011), .gt(comparator_2_gt), .eq(comparator_2_eq), .lt(comparator_2_lt));
  or or_1 (or_1_out, comparator_2_lt, comparator_2_gt);
  Decoder #(.select(5), .enable("false")) decoder_2 (
    .out0(decoder_2_out0[0]), .out1(decoder_2_out0[1]), .out2(decoder_2_out0[2]), .out3(decoder_2_out0[3]),
    .out4(decoder_2_out0[4]), .out5(decoder_2_out0[5]), .out6(decoder_2_out0[6]), .out7(decoder_2_out0[7]),
    .out8(decoder_2_out0[8]), .out9(decoder_2_out0[9]), .out10(decoder_2_out0[10]),
    .out11(decoder_2_out0[11]), .out12(decoder_2_out0[12]), .out13(decoder_2_out0[13]),
    .out14(decoder_2_out0[14]), .out15(decoder_2_out0[15]), .out16(decoder_2_out0[16]),
    .out17(decoder_2_out0[17]), .out18(decoder_2_out0[18]), .out19(decoder_2_out0[19]),
    .out20(decoder_2_out0[20]), .out21(decoder_2_out0[21]), .out22(decoder_2_out0[22]),
    .out23(decoder_2_out0[23]), .out24(decoder_2_out0[24]), .out25(decoder_2_out0[25]),
    .out26(decoder_2_out0[26]), .out27(decoder_2_out0[27]), .out28(decoder_2_out0[28]),
    .out29(decoder_2_out0[29]), .out30(decoder_2_out0[30]), .out31(decoder_2_out0[31]), .sel(leftbatY));
  Comparator #(.width(5)) comparator_3 (
    .a(chipID), .b(5'b11100), .gt(comparator_3_gt), .eq(comparator_3_eq), .lt(comparator_3_lt));
  or or_2 (or_2_out, comparator_3_lt, comparator_3_gt);
  Decoder #(.select(5), .enable("false")) decoder_3 (
    .out0(decoder_3_out0[0]), .out1(decoder_3_out0[1]), .out2(decoder_3_out0[2]), .out3(decoder_3_out0[3]),
    .out4(decoder_3_out0[4]), .out5(decoder_3_out0[5]), .out6(decoder_3_out0[6]), .out7(decoder_3_out0[7]),
    .out8(decoder_3_out0[8]), .out9(decoder_3_out0[9]), .out10(decoder_3_out0[10]),
    .out11(decoder_3_out0[11]), .out12(decoder_3_out0[12]), .out13(decoder_3_out0[13]),
    .out14(decoder_3_out0[14]), .out15(decoder_3_out0[15]), .out16(decoder_3_out0[16]),
    .out17(decoder_3_out0[17]), .out18(decoder_3_out0[18]), .out19(decoder_3_out0[19]),
    .out20(decoder_3_out0[20]), .out21(decoder_3_out0[21]), .out22(decoder_3_out0[22]),
    .out23(decoder_3_out0[23]), .out24(decoder_3_out0[24]), .out25(decoder_3_out0[25]),
    .out26(decoder_3_out0[26]), .out27(decoder_3_out0[27]), .out28(decoder_3_out0[28]),
    .out29(decoder_3_out0[29]), .out30(decoder_3_out0[30]), .out31(decoder_3_out0[31]), .sel(rightbatY));
  assign out_6 = rbat_t | lbat_t | ball;  // OR_Gate or_3, 32 bits wide
  or or_4 (or_4_out, comparator_1_lt, comparator_1_gt);
  Transistor #(.\type ("n"), .width(32)) transistor_1 (.in(decoder_1_out0), .out(ball), .gate(comparator_1_eq));
  Transistor #(.\type ("n"), .gate("br"), .width(32)) transistor_2 (.in({32{1'b0}}), .out(ball), .gate(or_4_out));
  // Probe on ball
  Multiplier #(.width(32)) multiplier_1 (.a(decoder_2_out0), .b(32'h7), .out(multiplier_1_out));  // open: cin, cout
  Multiplier #(.width(32)) multiplier_2 (.a(decoder_3_out0), .b(32'h7), .out(multiplier_2_out));  // open: cin, cout
  Adder #(.width(5)) adder_1 (.a(5'b00001), .b(chipID), .out(out_7));  // open: cin, cout
  Transistor #(.\type ("n"), .width(32)) transistor_3 (.in(multiplier_1_out), .out(lbat_t), .gate(comparator_2_eq));
  Transistor #(.\type ("n"), .gate("br"), .width(32)) transistor_4 (.in({32{1'b0}}), .out(lbat_t), .gate(or_1_out));
  Transistor #(.\type ("n"), .width(32)) transistor_5 (.in(multiplier_2_out), .out(rbat_t), .gate(comparator_3_eq));
  Transistor #(.\type ("n"), .gate("br"), .width(32)) transistor_6 (.in({32{1'b0}}), .out(rbat_t), .gate(or_2_out));
  // Probe on lbat_t
  // Probe on rbat_t

  assign out_8 = ballX;
  assign out_9 = ballY;
  assign out_10 = leftbatY;
  assign out_11 = rightbatY;
endmodule

module kinematic_controller (
  input  reset,
  input  down,
  input  up,
  input  [1:0] joystick,
  input  Choose_level,
  input  clock,
  output [4:0] chipID,
  output [4:0] ballX,
  output [4:0] ballY,
  output [4:0] leftbatY,
  output [4:0] rightbatY,
  output [4:0] rightBat,
  output [7:0] Rscores,
  output [7:0] Lscores
);

  wire adder_1_cout, adder_4_cout, adder_6_cout, adder_7_cout, and_3_out, and_4_out, and_5_out, and_6_out,
       and_7_out, and_8_out, and_9_out, and_10_out, and_11_out, and_13_out, and_14_out, and_15_out, colX,
       colY, comparator_1_eq, comparator_1_gt, comparator_1_lt, comparator_2_eq, comparator_2_gt,
       comparator_2_lt, comparator_3_eq, comparator_3_gt, comparator_3_lt, comparator_4_eq, comparator_4_gt,
       comparator_4_lt, comparator_5_eq, comparator_6_eq, comparator_7_eq, comparator_8_eq, hit,
       hit_detection_1_hit, hit_detection_2_hit, lScores_t, or_1_out, or_2_out, or_3_out, or_5_out, or_7_out,
       or_9_out, or_10_out, or_11_out, or_12_out, rScores_t;
  wire [2:0] negator_1_out, speedx, transistor_2_out, transistor_5_out, transistor_8_out, transistor_10_out,
       transistor_12_out, transistor_13_out, transistor_17_out, transistor_18_out, transistor_19_out;
  wire [4:0] adder_9_out, adder_12_out, register_7_q, register_8_q;
  wire [4:4] and_12_out, and_16_out;
  wire [7:0] adder_1_out, adder_2_out, adder_3_out, adder_4_out, adder_8_out, adder_10_out, register_1_q,
       register_2_q, register_5_q, register_6_q, transistor_1_out, transistor_4_out, Vx, Vy;
  wire [31:0] decoder_1_out0, decoder_2_out0;

  // Probe on transistor_1_out
  Transistor #(.\type ("n"), .width(8)) transistor_1 (.in(register_1_q), .out(transistor_1_out), .gate(colX));
  // Probe on register_1_q
  Transistor #(.\type ("n"), .gate("br"), .width(8)) transistor_2 (
    .in(8'h80), .out({ballX, transistor_2_out}), .gate(hit));
  Register register_1 (.D({ballX, transistor_2_out}), .Q(register_1_q), .clk(clock));  // open: en, clr
  Transistor #(.gate("br"), .width(8)) transistor_3 (
    .in(transistor_1_out), .out({ballX, transistor_2_out}), .gate(hit));
  // Probe on transistor_4_out
  Transistor #(.\type ("n"), .width(8)) transistor_4 (.in(register_2_q), .out(transistor_4_out), .gate(colY));
  Transistor #(.\type ("n"), .gate("br"), .width(8)) transistor_5 (
    .in(8'h80), .out({ballY, transistor_5_out}), .gate(hit));
  Transistor #(.gate("br"), .width(8)) transistor_6 (
    .in(transistor_4_out), .out({ballY, transistor_5_out}), .gate(hit));
  Transistor #(.width(8)) transistor_7 (.in(adder_1_out), .out(transistor_1_out), .gate(colX));
  Register register_2 (.D({ballY, transistor_5_out}), .Q(register_2_q), .clk(clock));  // open: en, clr
  // Probe on transistor_13_out
  // Probe on transistor_12_out
  Transistor #(.\type ("n"), .gate("br"), .width(3)) transistor_8 (
    .in({1'b0, Choose_level, 1'b1}), .out(transistor_8_out), .gate(hit));
  Transistor #(.gate("br"), .width(3)) transistor_9 (.in(transistor_12_out), .out(transistor_8_out), .gate(hit));
  Adder adder_1 (.a(register_1_q), .b({{6{Vx[7]}}, Vx[1:0]}), .out(adder_1_out), .cout(adder_1_cout));  // open: cin
  // Probe on {{6{Vx[7]}}, Vx[1:0]}
  Adder adder_2 (.a(8'he4), .b(register_1_q), .out(adder_2_out));  // open: cin, cout
  Transistor #(.\type ("n"), .gate("br"), .width(3)) transistor_10 (.in(speedx), .out(transistor_10_out), .gate(hit));
  Register #(.width(3)) register_3 (.D(transistor_10_out), .Q({Vx[7], Vx[1:0]}), .clk(clock));  // open: en, clr
  Transistor #(.gate("br"), .width(3)) transistor_11 (.in(transistor_13_out), .out(transistor_10_out), .gate(hit));
  Transistor #(.gate("br"), .width(3)) transistor_12 (.in({Vy[7], Vy[1:0]}), .out(transistor_12_out), .gate(colY));
  Register #(.width(3)) register_4 (.D(transistor_8_out), .Q({Vy[7], Vy[1:0]}), .clk(clock));  // open: en, clr
  // Probe on {Vy[7], Vy[1:0]}
  Comparator #(.mode("unsigned")) comparator_1 (
    .a({{6{Vx[7]}}, Vx[1:0]}), .b(8'h3), .gt(comparator_1_gt), .eq(comparator_1_eq), .lt(comparator_1_lt));
  or or_1 (or_1_out, comparator_1_eq, comparator_1_lt);
  Adder adder_3 (.a(8'h1c), .b(register_1_q), .out(adder_3_out));  // open: cin, cout
  Comparator #(.mode("unsigned")) comparator_2 (
    .a({{6{Vy[7]}}, Vy[1:0]}), .b(8'h3), .gt(comparator_2_gt), .eq(comparator_2_eq), .lt(comparator_2_lt));
  Adder adder_4 (.a(register_2_q), .b({{6{Vy[7]}}, Vy[1:0]}), .out(adder_4_out), .cout(adder_4_cout));  // open: cin
  Transistor #(.\type ("n"), .gate("br"), .width(3)) transistor_13 (
    .in(negator_1_out), .out(transistor_13_out), .gate(colX));
  Transistor #(.gate("br"), .width(3)) transistor_14 (.in({Vx[7], Vx[1:0]}), .out(transistor_13_out), .gate(colX));
  // Probe on {Vx[7], Vx[1:0]}
  Transistor #(.\type ("n"), .gate("br"), .width(3)) transistor_15 (
    .in(transistor_18_out), .out(transistor_12_out), .gate(colY));
  Adder #(.width(3)) adder_5 (.a({2'b00, Choose_level}), .b(3'b010), .out(speedx));  // open: cin, cout
  and and_1 (rScores_t, comparator_1_gt, ~adder_1_cout);  // AND_Gate
  and and_2 (lScores_t, or_1_out, adder_1_cout);
  Adder adder_6 (.a(adder_2_out), .b({{6{Vx[7]}}, Vx[1:0]}), .cout(adder_6_cout));  // open: out, cin
  Adder adder_7 (.a(adder_3_out), .b({{6{Vx[7]}}, Vx[1:0]}), .cout(adder_7_cout));  // open: out, cin
  or or_2 (or_2_out, comparator_2_eq, comparator_2_lt);
  // Probe on 3'b100
  Comparator #(.width(3), .mode("unsigned")) comparator_3 (
    .a(3'b100), .b({Vy[7], Vy[1:0]}), .gt(comparator_3_gt), .eq(comparator_3_eq), .lt(comparator_3_lt));
  // Probe on {{6{Vy[7]}}, Vy[1:0]}
  or or_3 (or_3_out, rScores_t, lScores_t);
  and and_3 (and_3_out, ~or_1_out, ~adder_6_cout);  // AND_Gate
  and and_4 (and_4_out, comparator_2_gt, ~adder_4_cout);  // AND_Gate
  or or_4 (colY, and_4_out, and_5_out);
  and and_5 (and_5_out, or_2_out, adder_4_cout);
  Comparator #(.width(3), .mode("unsigned")) comparator_4 (
    .a(3'b100), .b({Vx[7], Vx[1:0]}), .gt(comparator_4_gt), .eq(comparator_4_eq), .lt(comparator_4_lt));
  // Probe on {{6{Vx[7]}}, Vx[1:0]}
  or or_5 (or_5_out, comparator_3_gt, comparator_3_lt);
  or or_6 (hit, reset, or_3_out);
  and and_6 (and_6_out, ~comparator_1_gt, adder_7_cout);  // AND_Gate
  Transistor #(.width(8)) transistor_16 (.in(adder_4_out), .out(transistor_4_out), .gate(colY));
  or or_7 (or_7_out, comparator_4_gt, comparator_4_lt);
  Transistor #(.\type ("n"), .width(3)) transistor_17 (.in({Vy[7], Vy[1:0]}), .out(transistor_17_out), .gate(or_5_out));
  Transistor #(.\type ("n"), .width(3)) transistor_18 (.in(3'b011), .out(transistor_18_out), .gate(comparator_3_eq));
  and and_7 (and_7_out, ~hit, and_3_out);  // AND_Gate
  and and_8 (and_8_out, ~hit, and_6_out);  // AND_Gate
  Transistor #(.\type ("n"), .width(3)) transistor_19 (.in({Vx[7], Vx[1:0]}), .out(transistor_19_out), .gate(or_7_out));
  Negator #(.width(3)) negator_1 (.in(transistor_19_out), .out(negator_1_out));
  Transistor #(.\type ("n"), .width(3)) transistor_20 (.in(3'b011), .out(negator_1_out), .gate(comparator_4_eq));
  Negator #(.width(3)) negator_2 (.in(transistor_17_out), .out(transistor_18_out));
  hit_detection hit_detection_1 (.bat(leftbatY), .coll(and_7_out), .ballY(ballY), .hit(hit_detection_1_hit));
  hit_detection hit_detection_2 (.bat(rightbatY), .coll(and_8_out), .ballY(ballY), .hit(hit_detection_2_hit));
  or or_8 (colX, hit_detection_1_hit, hit_detection_2_hit);
  Register #(.trigger("falling")) register_5 (.D(Rscores), .Q(register_5_q), .clk(clock), .clr(reset));  // open: en
  Adder adder_8 (.a(8'h1), .b(register_5_q), .out(adder_8_out));  // open: cin, cout
  // Probe on joystick
  Transistor #(.\type ("n"), .width(8)) transistor_21 (.in(adder_8_out), .out(Rscores), .gate(rScores_t));
  Transistor #(.width(8)) transistor_22 (.in(register_5_q), .out(Rscores), .gate(rScores_t));
  and and_9 (and_9_out, ~joystick[1], joystick[0]);  // AND_Gate
  or or_9 (or_9_out, and_9_out, up);
  or or_10 (or_10_out, down, and_10_out);
  and and_10 (and_10_out, joystick[1], joystick[0]);
  and and_11 (and_11_out, ~comparator_5_eq, or_9_out, ~and_12_out[4]);  // AND_Gate
  and and_12 (and_12_out[4], ~and_11_out, or_10_out, ~comparator_6_eq);  // AND_Gate
  and and_13 (and_13_out, ~joystick[1], joystick[0]);  // AND_Gate
  or or_11 (or_11_out, and_13_out, up);
  or or_12 (or_12_out, down, and_14_out);
  and and_14 (and_14_out, joystick[1], joystick[0]);
  Register #(.trigger("falling")) register_6 (.D(Lscores), .Q(register_6_q), .clk(clock), .clr(reset));  // open: en
  and and_15 (and_15_out, ~comparator_7_eq, or_11_out, ~and_16_out[4]);  // AND_Gate
  and and_16 (and_16_out[4], ~and_15_out, or_12_out, ~comparator_8_eq);  // AND_Gate
  // Probe on register_7_q
  Adder #(.width(5)) adder_9 (
    .a(register_7_q), .b({5{and_12_out[4]}}), .out(adder_9_out), .cin(and_11_out));  // open: cout
  Register #(.width(5)) register_7 (.D(adder_9_out), .Q(register_7_q), .clk(clock), .clr(reset));  // open: en
  // Probe on ballX
  // Probe on ballY
  Adder adder_10 (.a(8'h1), .b(register_6_q), .out(adder_10_out));  // open: cin, cout
  Transistor #(.\type ("n"), .width(8)) transistor_23 (.in(adder_10_out), .out(Lscores), .gate(lScores_t));
  Adder #(.width(5)) adder_11 (.a(register_7_q), .b(5'b01111), .out(rightbatY));  // open: cin, cout
  Decoder #(.select(5), .enable("false")) decoder_1 (
    .out0(decoder_1_out0[0]), .out1(decoder_1_out0[1]), .out2(decoder_1_out0[2]), .out3(decoder_1_out0[3]),
    .out4(decoder_1_out0[4]), .out5(decoder_1_out0[5]), .out6(decoder_1_out0[6]), .out7(decoder_1_out0[7]),
    .out8(decoder_1_out0[8]), .out9(decoder_1_out0[9]), .out10(decoder_1_out0[10]),
    .out11(decoder_1_out0[11]), .out12(decoder_1_out0[12]), .out13(decoder_1_out0[13]),
    .out14(decoder_1_out0[14]), .out15(decoder_1_out0[15]), .out16(decoder_1_out0[16]),
    .out17(decoder_1_out0[17]), .out18(decoder_1_out0[18]), .out19(decoder_1_out0[19]),
    .out20(decoder_1_out0[20]), .out21(decoder_1_out0[21]), .out22(decoder_1_out0[22]),
    .out23(decoder_1_out0[23]), .out24(decoder_1_out0[24]), .out25(decoder_1_out0[25]),
    .out26(decoder_1_out0[26]), .out27(decoder_1_out0[27]), .out28(decoder_1_out0[28]),
    .out29(decoder_1_out0[29]), .out30(decoder_1_out0[30]), .out31(decoder_1_out0[31]));  // open: sel
  Decoder #(.select(5), .enable("false")) decoder_2 (
    .out0(decoder_2_out0[0]), .out1(decoder_2_out0[1]), .out2(decoder_2_out0[2]), .out3(decoder_2_out0[3]),
    .out4(decoder_2_out0[4]), .out5(decoder_2_out0[5]), .out6(decoder_2_out0[6]), .out7(decoder_2_out0[7]),
    .out8(decoder_2_out0[8]), .out9(decoder_2_out0[9]), .out10(decoder_2_out0[10]),
    .out11(decoder_2_out0[11]), .out12(decoder_2_out0[12]), .out13(decoder_2_out0[13]),
    .out14(decoder_2_out0[14]), .out15(decoder_2_out0[15]), .out16(decoder_2_out0[16]),
    .out17(decoder_2_out0[17]), .out18(decoder_2_out0[18]), .out19(decoder_2_out0[19]),
    .out20(decoder_2_out0[20]), .out21(decoder_2_out0[21]), .out22(decoder_2_out0[22]),
    .out23(decoder_2_out0[23]), .out24(decoder_2_out0[24]), .out25(decoder_2_out0[25]),
    .out26(decoder_2_out0[26]), .out27(decoder_2_out0[27]), .out28(decoder_2_out0[28]),
    .out29(decoder_2_out0[29]), .out30(decoder_2_out0[30]), .out31(decoder_2_out0[31]));  // open: sel
  Transistor #(.width(8)) transistor_24 (.in(register_6_q), .out(Lscores), .gate(lScores_t));
  // Probe on register_8_q
  Adder #(.width(5)) adder_12 (
    .a(register_8_q), .b({5{and_16_out[4]}}), .out(adder_12_out), .cin(and_15_out));  // open: cout
  Register #(.width(5)) register_8 (.D(adder_12_out), .Q(register_8_q), .clk(clock), .clr(reset));  // open: en
  // Probe on rightbatY
  Comparator #(.width(5), .mode("unsigned")) comparator_5 (
    .a(5'b11101), .b(rightbatY), .eq(comparator_5_eq));  // open: gt, lt
  Comparator #(.width(5), .mode("unsigned")) comparator_6 (
    .a(rightbatY), .b({5{1'b0}}), .eq(comparator_6_eq));  // open: gt, lt
  Adder #(.width(5)) adder_13 (.a(register_8_q), .b(5'b01111), .out(leftbatY));  // open: cin, cout
  // Probe on ballX
  // Probe on ballY
  // Probe on leftbatY
  Comparator #(.width(5), .mode("unsigned")) comparator_7 (
    .a(5'b11101), .b(leftbatY), .eq(comparator_7_eq));  // open: gt, lt
  Comparator #(.width(5), .mode("unsigned")) comparator_8 (
    .a(leftbatY), .b({5{1'b0}}), .eq(comparator_8_eq));  // open: gt, lt

  assign chipID = {5{1'b0}};

  // Other names for the same wires on the sheet: newX[4:0] = ballX; newY[4:0] = ballY; speedy[1] = Choose_level;
  //   clk = clock; lBat[4:0] = leftbatY; rBat[4:0] = rightbatY; Vx[6:2] = {5{Vx[7]}}; Vy[6:2] = {5{Vy[7]}}
endmodule

module hit_detection (
  input  [4:0] bat,
  input  [4:0] ballY,
  input  coll,
  output hit
);

  wire and_4_out, or_3_out, or_4_out;
  wire [2:0] and_5_out, and_6_out, speedy;
  wire [2:2] and_3_out, not_1_out;
  wire [31:0] and_1_out, and_2_out, decoder_1_out0, decoder_2_out0, decoder_3_out0, decoder_4_out0, or_2_out,
       shifter_1_out, shifter_2_out, shifter_3_out;

  Decoder #(.select(5), .enable("false")) decoder_1 (
    .out0(decoder_1_out0[0]), .out1(decoder_1_out0[1]), .out2(decoder_1_out0[2]), .out3(decoder_1_out0[3]),
    .out4(decoder_1_out0[4]), .out5(decoder_1_out0[5]), .out6(decoder_1_out0[6]), .out7(decoder_1_out0[7]),
    .out8(decoder_1_out0[8]), .out9(decoder_1_out0[9]), .out10(decoder_1_out0[10]),
    .out11(decoder_1_out0[11]), .out12(decoder_1_out0[12]), .out13(decoder_1_out0[13]),
    .out14(decoder_1_out0[14]), .out15(decoder_1_out0[15]), .out16(decoder_1_out0[16]),
    .out17(decoder_1_out0[17]), .out18(decoder_1_out0[18]), .out19(decoder_1_out0[19]),
    .out20(decoder_1_out0[20]), .out21(decoder_1_out0[21]), .out22(decoder_1_out0[22]),
    .out23(decoder_1_out0[23]), .out24(decoder_1_out0[24]), .out25(decoder_1_out0[25]),
    .out26(decoder_1_out0[26]), .out27(decoder_1_out0[27]), .out28(decoder_1_out0[28]),
    .out29(decoder_1_out0[29]), .out30(decoder_1_out0[30]), .out31(decoder_1_out0[31]), .sel(bat));
  Decoder #(.select(5), .enable("false")) decoder_2 (
    .out0(decoder_2_out0[0]), .out1(decoder_2_out0[1]), .out2(decoder_2_out0[2]), .out3(decoder_2_out0[3]),
    .out4(decoder_2_out0[4]), .out5(decoder_2_out0[5]), .out6(decoder_2_out0[6]), .out7(decoder_2_out0[7]),
    .out8(decoder_2_out0[8]), .out9(decoder_2_out0[9]), .out10(decoder_2_out0[10]),
    .out11(decoder_2_out0[11]), .out12(decoder_2_out0[12]), .out13(decoder_2_out0[13]),
    .out14(decoder_2_out0[14]), .out15(decoder_2_out0[15]), .out16(decoder_2_out0[16]),
    .out17(decoder_2_out0[17]), .out18(decoder_2_out0[18]), .out19(decoder_2_out0[19]),
    .out20(decoder_2_out0[20]), .out21(decoder_2_out0[21]), .out22(decoder_2_out0[22]),
    .out23(decoder_2_out0[23]), .out24(decoder_2_out0[24]), .out25(decoder_2_out0[25]),
    .out26(decoder_2_out0[26]), .out27(decoder_2_out0[27]), .out28(decoder_2_out0[28]),
    .out29(decoder_2_out0[29]), .out30(decoder_2_out0[30]), .out31(decoder_2_out0[31]), .sel(ballY));
  Decoder #(.select(5), .enable("false")) decoder_3 (
    .out0(decoder_3_out0[0]), .out1(decoder_3_out0[1]), .out2(decoder_3_out0[2]), .out3(decoder_3_out0[3]),
    .out4(decoder_3_out0[4]), .out5(decoder_3_out0[5]), .out6(decoder_3_out0[6]), .out7(decoder_3_out0[7]),
    .out8(decoder_3_out0[8]), .out9(decoder_3_out0[9]), .out10(decoder_3_out0[10]),
    .out11(decoder_3_out0[11]), .out12(decoder_3_out0[12]), .out13(decoder_3_out0[13]),
    .out14(decoder_3_out0[14]), .out15(decoder_3_out0[15]), .out16(decoder_3_out0[16]),
    .out17(decoder_3_out0[17]), .out18(decoder_3_out0[18]), .out19(decoder_3_out0[19]),
    .out20(decoder_3_out0[20]), .out21(decoder_3_out0[21]), .out22(decoder_3_out0[22]),
    .out23(decoder_3_out0[23]), .out24(decoder_3_out0[24]), .out25(decoder_3_out0[25]),
    .out26(decoder_3_out0[26]), .out27(decoder_3_out0[27]), .out28(decoder_3_out0[28]),
    .out29(decoder_3_out0[29]), .out30(decoder_3_out0[30]), .out31(decoder_3_out0[31]), .sel(bat));
  Decoder #(.select(5), .enable("false")) decoder_4 (
    .out0(decoder_4_out0[0]), .out1(decoder_4_out0[1]), .out2(decoder_4_out0[2]), .out3(decoder_4_out0[3]),
    .out4(decoder_4_out0[4]), .out5(decoder_4_out0[5]), .out6(decoder_4_out0[6]), .out7(decoder_4_out0[7]),
    .out8(decoder_4_out0[8]), .out9(decoder_4_out0[9]), .out10(decoder_4_out0[10]),
    .out11(decoder_4_out0[11]), .out12(decoder_4_out0[12]), .out13(decoder_4_out0[13]),
    .out14(decoder_4_out0[14]), .out15(decoder_4_out0[15]), .out16(decoder_4_out0[16]),
    .out17(decoder_4_out0[17]), .out18(decoder_4_out0[18]), .out19(decoder_4_out0[19]),
    .out20(decoder_4_out0[20]), .out21(decoder_4_out0[21]), .out22(decoder_4_out0[22]),
    .out23(decoder_4_out0[23]), .out24(decoder_4_out0[24]), .out25(decoder_4_out0[25]),
    .out26(decoder_4_out0[26]), .out27(decoder_4_out0[27]), .out28(decoder_4_out0[28]),
    .out29(decoder_4_out0[29]), .out30(decoder_4_out0[30]), .out31(decoder_4_out0[31]), .sel(ballY));
  Shifter #(.width(32)) shifter_1 (.in(decoder_3_out0), .\dist (5'b00001), .out(shifter_1_out));
  Shifter #(.width(32)) shifter_2 (.in(decoder_1_out0), .\dist (5'b00001), .out(shifter_2_out));
  Shifter #(.width(32)) shifter_3 (.in(shifter_1_out), .\dist (5'b00001), .out(shifter_3_out));
  // OR_Gate or_1 has open pins: in0=decoder_1_out0, in2=shifter_2_out, out=open
  assign or_2_out = decoder_3_out0 | shifter_1_out | shifter_3_out;  // OR_Gate or_2, 32 bits wide
  // Probe on or_2_out
  assign and_1_out = decoder_1_out0 & decoder_2_out0;  // AND_Gate and_1, 32 bits wide
  assign and_2_out = or_2_out & decoder_4_out0;  // AND_Gate and_2, 32 bits wide
  or or_3 (or_3_out, and_1_out[0], and_1_out[1], and_1_out[2], and_1_out[3], and_1_out[4], and_1_out[5], and_1_out[6], and_1_out[7], and_1_out[8], and_1_out[9], and_1_out[10], and_1_out[11], and_1_out[12], and_1_out[13], and_1_out[14], and_1_out[15], and_1_out[16], and_1_out[17], and_1_out[18], and_1_out[19], and_1_out[20], and_1_out[21], and_1_out[22], and_1_out[23], and_1_out[24], and_1_out[25], and_1_out[26], and_1_out[27], and_1_out[28], and_1_out[29], and_1_out[30], and_1_out[31]);
  or or_4 (or_4_out, and_2_out[0], and_2_out[1], and_2_out[2], and_2_out[3], and_2_out[4], and_2_out[5], and_2_out[6], and_2_out[7], and_2_out[8], and_2_out[9], and_2_out[10], and_2_out[11], and_2_out[12], and_2_out[13], and_2_out[14], and_2_out[15], and_2_out[16], and_2_out[17], and_2_out[18], and_2_out[19], and_2_out[20], and_2_out[21], and_2_out[22], and_2_out[23], and_2_out[24], and_2_out[25], and_2_out[26], and_2_out[27], and_2_out[28], and_2_out[29], and_2_out[30], and_2_out[31]);
  and and_3 (and_3_out[2], or_3_out, coll);
  and and_4 (and_4_out, or_4_out, coll);
  not not_1 (not_1_out[2], and_3_out[2]);
  assign and_5_out = 3'b011 & {3{not_1_out[2]}};  // AND_Gate and_5, 3 bits wide
  assign and_6_out = {3{and_3_out[2]}} & 3'b111;  // AND_Gate and_6, 3 bits wide
  assign speedy = and_5_out | and_6_out;  // OR_Gate or_5, 3 bits wide
  or or_6 (hit, and_3_out[2], and_4_out);
  Pull_Resistor pull_resistor_1 (.node(hit));

  // Notes on the sheet:
  //   Для проверки, что мячик ударился об нижний пиксель
  //   Селектор для выбора скорости. Если мяч попадает в нижний бит, то скорость меняется 
endmodule
